# Fritzing sketch ArduinoSchaltplan (saved by Fritzing 0.9.3b)
breadboards: 2

parts:
  Bauteil1 = Arduino Mega ADK (Rev3)
  Bauteil2 = Soil Moisture Sensor
  R1 = Resistor [tolerance=±5% resistance=1k package="0603 [SMD]"]
  U1 = TRANSISTOR_NPN_2 [package=to-92]
  U2 = LCD-16X2 [package=lcd-16x2]
  R2 = Trimmer Potentiometer [maximum_resistance=10kΩ package=THT]
  R3 = Resistor [tolerance=±5% resistance=220 package="2010 [SMD]"]
  R4 = PHOTOCELL [package=photocell-kit]
  RHT1 = Humidity and Temperature Sensor RHT03  # not connected
  R5 = Resistor [tolerance=±5% resistance=10k package=THT]

nets:
  N1: Bauteil1.A0, Bauteil2.SIG
  N2: Bauteil1.D13_PWM, U2.RS
  N3: Bauteil1.D12_PWM, U2.E
  5V: Bauteil1.5V, U1.E, U2.VDD, R2.leg2, R3.Pin_1
  GND: Bauteil1.GND, Bauteil2.GND, U2.VSS, U2.R_W, U2.K, R2.leg1
  N4: Bauteil1.D4_PWM, U2.DB7
  N5: Bauteil1.D5_PWM, U2.DB6
  N6: Bauteil1.D6_PWM, U2.DB5
  N7: Bauteil1.D7_PWM, U2.DB4
  N8: Bauteil1.D52/SCK, R1.Pin_0
  N9: Bauteil2.VCC, U1.C
  N10: R1.Pin_1, U1.B
  N11: U2.VO, R2.wiper
  N12: U2.A, R3.Pin_0
  N13: R4.P$1, R5.Pin_1
